# Fritzing sketch full diagram (saved by Fritzing 0.9.3b)

parts:
  Motor1_joint1 = DC Motor
  Motor2_joint1 = DC Motor
  Motor2_joint_2 = DC Motor
  Motor1_rotating_base = DC Motor
  Motor1_joint_2 = DC Motor
  L298N1_joint_1_and_2 = L298_BRIDGE_DRIVER [package=powerso20]
  L298N2_rotating_base_+telescopic_arm_(12v) = L298_BRIDGE_DRIVER [package=powerso20]
  Motor2_rotating_base = DC Motor
  L298N3_joint_4_and_5 = L298_BRIDGE_DRIVER [package=powerso20]
  Motor_joint_4 = DC Motor
  Motor_telescopic_arm_joint_3 = DC Motor
  L298N2_joint_3_(24v) = L298_BRIDGE_DRIVER [package=powerso20]
  Motor_joint_3 = DC Motor
  Motor_joint_5 = DC Motor
  L298N3_joint_6 = L298_BRIDGE_DRIVER [package=powerso20]
  Motor_joint_6 = DC Motor
  Power_supply = DC Power [voltage=24V]
  Power_supply1 = DC Power [voltage=12V]
  Componente2 = 9-DOF Absolute Orientation IMU Fusion Breakout - BNO055
  Onderdeel1 = Arduino Nano (Rev3.0) (ICSP)
  Onderdeel2 = Arduino Uno (Rev3)
  Power_supply2 = DC Power [voltage=12V]
  Componente3 = 9-DOF Absolute Orientation IMU Fusion Breakout - BNO055

nets:
  AI ()/AI()/DI ()/DI(): Motor1_joint1.pin_1, Motor2_joint1.pin_2, Motor2_joint_2.pin_2, Motor1_joint_2.pin_1, L298N1_joint_1_and_2.OUT2, L298N1_joint_1_and_2.IN1, L298N1_joint_1_and_2.IN2, L298N1_joint_1_and_2.IN3, L298N1_joint_1_and_2.IN4, L298N1_joint_1_and_2.OUT3, L298N2_rotating_base_+telescopic_arm_(12v).IN1, L298N2_rotating_base_+telescopic_arm_(12v).IN2, L298N2_rotating_base_+telescopic_arm_(12v).IN3, L298N2_rotating_base_+telescopic_arm_(12v).IN4, L298N3_joint_4_and_5.OUT1, L298N3_joint_4_and_5.IN1, L298N3_joint_4_and_5.IN2, L298N3_joint_4_and_5.IN3, L298N3_joint_4_and_5.IN4, L298N3_joint_4_and_5.OUT4, Motor_joint_4.pin_2, L298N2_joint_3_(24v).OUT1, L298N2_joint_3_(24v).IN1, L298N2_joint_3_(24v).IN2, Motor_joint_3.pin_2, Motor_joint_5.pin_2, L298N3_joint_6.OUT1, L298N3_joint_6.IN1, L298N3_joint_6.IN2, Motor_joint_6.pin_2, Componente2.GND, Onderdeel1.GND, Onderdeel2.GND, Power_supply2.V-, Componente3.GND
  VIN: Motor1_joint1.pin_2, Motor2_joint1.pin_1, Motor2_joint_2.pin_1, Motor1_joint_2.pin_2, L298N1_joint_1_and_2.OUT1, L298N1_joint_1_and_2.OUT4, L298N3_joint_4_and_5.OUT2, L298N3_joint_4_and_5.OUT3, Motor_joint_4.pin_1, L298N2_joint_3_(24v).OUT2, Motor_joint_3.pin_1, Motor_joint_5.pin_1, L298N3_joint_6.OUT2, Motor_joint_6.pin_1, Onderdeel1.VIN, Onderdeel2.VIN, Power_supply2.V+
  N1: Motor1_rotating_base.pin_1, L298N2_rotating_base_+telescopic_arm_(12v).OUT2, Motor2_rotating_base.pin_1
  N2: Motor1_rotating_base.pin_2, L298N2_rotating_base_+telescopic_arm_(12v).OUT1, Motor2_rotating_base.pin_2
  GND: L298N1_joint_1_and_2.GND, L298N2_joint_3_(24v).GND, Power_supply.V-
  N3: L298N1_joint_1_and_2.VS, L298N2_joint_3_(24v).VS, Power_supply.V+
  plcPWM (): L298N1_joint_1_and_2.ENA, L298N1_joint_1_and_2.ENB, L298N2_rotating_base_+telescopic_arm_(12v).ENA, L298N2_rotating_base_+telescopic_arm_(12v).ENB, L298N3_joint_4_and_5.ENA, L298N3_joint_4_and_5.ENB, L298N2_joint_3_(24v).ENA, L298N3_joint_6.ENA
  GND_2: L298N2_rotating_base_+telescopic_arm_(12v).GND, L298N3_joint_4_and_5.GND, L298N3_joint_6.GND, Power_supply1.V-
  N4: L298N2_rotating_base_+telescopic_arm_(12v).VS, L298N3_joint_4_and_5.VS, L298N3_joint_6.VS, Power_supply1.V+
  N5: L298N2_rotating_base_+telescopic_arm_(12v).OUT3, Motor_telescopic_arm_joint_3.pin_1
  N6: L298N2_rotating_base_+telescopic_arm_(12v).OUT4, Motor_telescopic_arm_joint_3.pin_2
  N7: Componente2.5.0V, Onderdeel1.5V
  N8: Onderdeel2.A4/SDA, Componente3.SDA_5V
  N9: Onderdeel2.A5/SCL, Componente3.SCL_5V
  N10: Onderdeel2.5V, Componente3.5.0V

custom parts:
  9-DOF Absolute Orientation IMU Fusion Breakout - BNO055: A MEMS accelerometer, magnetometer and gyroscope on a single die with a high speed ARM Cortex-M0 based processor to digest all the sensor data, abstract the sensor fusion and real time requirements away, and spit out data you can use in quaternions, Euler angles or vectors.
